# Fritzing sketch PainelDojo (saved by Fritzing 0.9.3b)
breadboards: 1

parts:
  7_Segment1 = 7 Segment Display
  IC1 = ULN2803A [package=THT]
  R2 = Resistor [tolerance=±5% resistance=150 package="0402 [SMD]"]
  R3 = Resistor [tolerance=±5% resistance=150 package="0402 [SMD]"]
  R4 = Resistor [tolerance=±5% resistance=150 package="0402 [SMD]"]
  R5 = Resistor [tolerance=±5% resistance=150 package="0402 [SMD]"]
  R6 = Resistor [tolerance=±5% resistance=150 package="0402 [SMD]"]
  R7 = Resistor [tolerance=±5% resistance=150 package="0402 [SMD]"]
  R8 = Resistor [tolerance=±5% resistance=150 package="0402 [SMD]"]
  R9 = Resistor [tolerance=±5% resistance=1k package="0402 [SMD]"]
  Componente1 = Arduino Uno (Rev3)
  J1 = Power Jack [package=power_jack_combo]
  R1 = Rotary Potentiometer (Small) [maximum_resistance=100kΩ package=THT]

nets:
  N1: 7_Segment1.Segment_E, R2.Pin_0
  N2: 7_Segment1.Segment_D, R8.Pin_0
  N3: 7_Segment1.common_anode, J1.PWR
  N4: 7_Segment1.Segment_C, R7.Pin_0
  N5: 7_Segment1.Segment_DP, R9.Pin_0
  N6: 7_Segment1.Segment_B, R3.Pin_0
  N7: 7_Segment1.Segment_A, R4.Pin_0
  N8: 7_Segment1.Segment_F, R5.Pin_0
  N9: 7_Segment1.Segment_G, R6.Pin_0
  N10: IC1.In_1, Componente1.D13/SCK
  N11: IC1.In_2, Componente1.D8
  N12: IC1.In_3, Componente1.D7
  N13: IC1.In_4, Componente1.D6_PWM
  N14: IC1.In_5, Componente1.D5_PWM
  N15: IC1.In_6, Componente1.D4
  N16: IC1.In_7, Componente1.D3_PWM
  N17: IC1.In_8, Componente1.D2
  GND: IC1.0V, Componente1.GND, J1.GND, R1.leg1
  N18: IC1.Out_8, R2.Pin_1
  N19: IC1.Out_7, R8.Pin_1
  N20: IC1.Out_6, R7.Pin_1
  N21: IC1.Out_5, R6.Pin_1
  N22: IC1.Out_4, R5.Pin_1
  N23: IC1.Out_3, R4.Pin_1
  N24: IC1.Out_2, R3.Pin_1
  N25: IC1.Out_1, R9.Pin_1
  N26: Componente1.A0, R1.wiper
  N27: Componente1.5V, R1.leg2

notes:
  Coding Dojo Arduino
